# Fritzing sketch load_cells (saved by Fritzing 0.9.10b)

parts:
  A+ = Load Sensor - 50kg [part_number=SEN-10245]
  E+ = Load Sensor - 50kg [part_number=SEN-10245]
  A- = Load Sensor - 50kg [part_number=SEN-10245]
  E- = Load Sensor - 50kg [part_number=SEN-10245]
  Mod1 = Amica NodeMCU DEVKIT 1.0
  HX711 = HX711 Weighing Sensor Module

nets (from the schematic view):
  N1: A+.B, E+.B
  N2: A+.W, E-.W
  N3: A+.R, HX711.A+
  N4: E+.W, A-.W
  N5: E+.R, HX711.E+
  N6: A-.B, E-.B
  N7: A-.R, HX711.A-
  N8: E-.R, HX711.E-
  N9: Mod1.pin1, Mod1.pin_26, HX711.VCC
  N10: Mod1.pin_13, HX711.DO/RX
  N11: Mod1.pin_14, HX711.CK/TX
  N12: Mod1.pin_25, HX711.GND

custom parts:
  Load Sensor - 50kg: Half-wheatstone bridge Load Cell modified from the Fritzing Repo This load sensor, sometimes called a strain gauge, is the same one found in digital bathroom scales (you know, the ones you use in January for your New Year's resolutions, and then forget about a month later). This sensor can measure up to about 110 pounds.
