# Fritzing sketch photoresistor (saved by Fritzing 0.9.10b)
breadboards: 1

parts:
  R1 = PHOTOCELL [package=photocell]
  Mod1 = Amica NodeMCU DEVKIT 1.0
  R2 = Resistor [tolerance=±5% resistance=1000 power=0.25 package="2512 [SMD]"]

nets:
  N1: R1.P$1, Mod1.pin_30
  N2: R1.P$2, Mod1.pin_16, R2.Pin_1
  N3: Mod1.pin2, R2.Pin_0
