# Fritzing sketch rfid_scanner (saved by Fritzing 0.9.10b)
breadboards: 1

parts:
  Mod1 = Amica NodeMCU DEVKIT 1.0
  U1 = RFID RC522 SIP - 8 pins [chip_label="RFID RC522" package="SIP (Single Inline) [THT]"]

nets:
  N1: Mod1.pin1, U1.VCC
  N2: Mod1.pin2, U1.GND
  N3: Mod1.pin5, U1.NSS
  N4: Mod1.pin6, U1.MOSI
  N5: Mod1.pin7, U1.MISO
  N6: Mod1.pin8, U1.SCK
  N7: Mod1.pin_12, U1.RST

custom parts:
  RFID RC522 SIP - 8 pins: A SIP stand-in part for RFID RC522 . With 8 pins on a 300 mil single inline package (SIP) footprint.
