# Fritzing sketch servo_motor (saved by Fritzing 0.9.10b)

parts:
  Mod1 = Amica NodeMCU DEVKIT 1.0
  SERVO1 = Tower Pro SG90 servo [part_number=101246]
  BAT1 = Battery Holders [package=battery-aa]

nets:
  N1: Mod1.pin2, Mod1.pin_25, Mod1.pin_29, SERVO1.GND, BAT1.-
  N2: Mod1.pin_15, SERVO1.Signal
  N3: SERVO1.+5V, BAT1.+

custom parts:
  Tower Pro SG90 servo: Original file by John De Cristofaro http://www.adafruit.com/products/1449 Adafruit Feedback Servo (Small) Edited by: e-radionica.com 28/9/2015
